// Logisim project The_Forge.circ as structural Verilog: 5 circuits, main circuit main
module registerFile (
  input  Clock,
  input  [1:0] ReadReg1,
  input  [1:0] WriteReg,
  input  RegWrite,
  input  [7:0] RegDataW,
  input  [1:0] ReadReg2,
  output [7:0] Reg1,
  output [7:0] Reg2,
  output [7:0] Reg3,
  output [7:0] Reg4,
  output [7:0] RegData1,
  output [7:0] RegData2
);

  wire and_1_out, and_2_out, and_3_out, and_4_out, decoder_1_out0, decoder_1_out1, decoder_1_out2,
       decoder_1_out3;

  Decoder #(.enable("false"), .select(2)) decoder_1 (
    .out0(decoder_1_out0), .out1(decoder_1_out1), .out2(decoder_1_out2), .out3(decoder_1_out3), .sel(WriteReg));
  Register #(.trigger("falling")) X0 (.D(RegDataW), .en(and_1_out), .clk(Clock), .Q(Reg1));  // open: clr
  and and_1 (and_1_out, RegWrite, decoder_1_out0);
  Register #(.trigger("falling")) X1 (.D(RegDataW), .en(and_2_out), .clk(Clock), .Q(Reg2));  // open: clr
  and and_2 (and_2_out, RegWrite, decoder_1_out1);
  Register #(.trigger("falling")) X2 (.D(RegDataW), .en(and_3_out), .clk(Clock), .Q(Reg3));  // open: clr
  and and_3 (and_3_out, RegWrite, decoder_1_out2);
  Register #(.trigger("falling")) X3 (.D(RegDataW), .en(and_4_out), .clk(Clock), .Q(Reg4));  // open: clr
  and and_4 (and_4_out, RegWrite, decoder_1_out3);
  Multiplexer #(.select(2), .width(8)) multiplexer_1 (
    .in0(Reg1), .in1(Reg2), .in2(Reg3), .in3(Reg4), .out(RegData1), .sel(ReadReg1));
  Multiplexer #(.select(2), .width(8)) multiplexer_2 (
    .in0(Reg1), .in1(Reg2), .in2(Reg3), .in3(Reg4), .out(RegData2), .sel(ReadReg2));
endmodule

module ALU (
  input  [7:0] input1,
  input  [7:0] input2,
  input  OP,
  output [7:0] ALU_output
);

  wire [7:0] adder_1_out, subtractor_1_out;

  Adder adder_1 (.a(input1), .b(input2), .out(adder_1_out));  // open: cin, cout
  Subtractor subtractor_1 (.a(input1), .b(input2), .out(subtractor_1_out));  // open: bin, bout
  Multiplexer #(.width(8)) multiplexer_1 (.in0(adder_1_out), .in1(subtractor_1_out), .out(ALU_output), .sel(OP));

  // Notes on the sheet:
  //   Input 1(A)
  //   Input 2(B)
endmodule

module main (
  output [1:0] out_1,
  output [7:0] out_2,
  output [7:0] out_3
);

  wire clock_1_out, decode_1_out_6, memcontrol_1_read_trig, memcontrol_1_write_trig;
  wire [1:0] decode_1_rd, decode_1_rm, decode_1_rn;
  wire [3:0] registerfile_1_reg1, registerfile_1_reg1_2, registerfile_1_reg2, registerfile_1_reg2_2,
       registerfile_1_reg3, registerfile_1_reg3_2, registerfile_1_reg4, registerfile_1_reg4_2;
  wire [7:0] adder_1_out, alu_1_alu_output, instruction_dout, register_1_q, registerfile_1_regdata1,
       registerfile_1_regdata2;

  Clock clock_1 (.out(clock_1_out));
  Register register_1 (.D(adder_1_out), .clk(clock_1_out), .Q(register_1_q));  // open: en, clr
  Adder adder_1 (.a(8'h1), .b(register_1_q), .out(adder_1_out));  // open: cin, cout
  RAM #(.trigger("high")) ram_1 (
    .addr(registerfile_1_regdata1), .we(memcontrol_1_write_trig), .oe(memcontrol_1_read_trig),
    .din(registerfile_1_regdata2), .dout(out_3));
  memControl memcontrol_1 (.OP_in(out_1), .Write_Trig(memcontrol_1_write_trig), .read_Trig(memcontrol_1_read_trig));
  RAM #(.enables("line")) instruction (
    .addr(register_1_q), .clk(clock_1_out), .dout(instruction_dout));  // open: we, din
  decode decode_1 (
    .in_1(instruction_dout), .RD(decode_1_rd), .Rn(decode_1_rn), .Rm(decode_1_rm), .Opcode(out_1),
    .out_6(decode_1_out_6));
  ALU alu_1 (
    .input1(registerfile_1_regdata1), .input2(registerfile_1_regdata2), .OP(out_1[0]),
    .ALU_output(alu_1_alu_output));
  Multiplexer #(.select(2), .width(8)) multiplexer_1 (
    .in0(alu_1_alu_output), .in1(alu_1_alu_output), .in2(out_3), .in3({8{1'b0}}), .out(out_2), .sel(out_1));
  Hex_Digit_Display hex_digit_display_1 (.value(registerfile_1_reg1_2));  // open: dp
  Hex_Digit_Display hex_digit_display_2 (.value(registerfile_1_reg1));  // open: dp
  registerFile registerfile_1 (
    .Clock(clock_1_out), .ReadReg1(decode_1_rn), .WriteReg(decode_1_rd), .RegWrite(decode_1_out_6),
    .RegDataW(out_2), .ReadReg2(decode_1_rm), .Reg1({registerfile_1_reg1_2, registerfile_1_reg1}),
    .Reg2({registerfile_1_reg2_2, registerfile_1_reg2}), .Reg3({registerfile_1_reg3_2, registerfile_1_reg3}),
    .Reg4({registerfile_1_reg4_2, registerfile_1_reg4}), .RegData1(registerfile_1_regdata1),
    .RegData2(registerfile_1_regdata2));
  Hex_Digit_Display hex_digit_display_3 (.value(registerfile_1_reg2_2));  // open: dp
  Hex_Digit_Display hex_digit_display_4 (.value(registerfile_1_reg2));  // open: dp
  Hex_Digit_Display hex_digit_display_5 (.value(registerfile_1_reg3_2));  // open: dp
  Hex_Digit_Display hex_digit_display_6 (.value(registerfile_1_reg3));  // open: dp
  Hex_Digit_Display hex_digit_display_7 (.value(registerfile_1_reg4_2));  // open: dp
  Hex_Digit_Display hex_digit_display_8 (.value(registerfile_1_reg4));  // open: dp

  // Notes on the sheet:
  //   The Forge
  //   By Dylan McGrory and Nick Fontana
  //   I pledge my honor that I have abided by the Stevens Honor System.
  //   Registers:
  //   0
  //   1
  //   2
  //   3
endmodule

module decode (
  input  [7:0] in_1,
  output [1:0] RD,
  output [1:0] Rn,
  output [1:0] Rm,
  output [1:0] Opcode,
  output out_6
);

  wire and_1_out;

  and and_1 (and_1_out, in_1[6], in_1[7]);
  not not_1 (out_6, and_1_out);

  assign Opcode = in_1[7:6];
  assign RD = in_1[1:0];
  assign Rm = in_1[5:4];
  assign Rn = in_1[3:2];
endmodule

module memControl (
  input  [1:0] OP_in,
  output Write_Trig,
  output read_Trig
);

  wire not_1_out;

  not not_1 (not_1_out, OP_in[0]);
  and and_1 (Write_Trig, OP_in[0], OP_in[1]);
  and and_2 (read_Trig, not_1_out, OP_in[1]);
endmodule
